// Logisim project pipelined.circ as structural Verilog: 34 circuits, main circuit main
module main (
);

  wire and_1_out, button_1_out, clock_1_out, ex_mem_latch_1_memread_2, ex_section_1_branch,
       hazarddetect_1_hazard, id_ex_latch_1_memread_2, id_ex_latch_1_memwrite_2, id_ex_latch_1_subop_2,
       id_section_1_memread, id_section_1_memwrite, id_section_1_subop, not_1_out, or_1_out, or_2_out,
       wb_section_1_halt, wb_section_1_writeenable;
  wire [1:0] forwardunit_1_ctrl_a, forwardunit_1_ctrl_b;
  wire [2:0] ex_mem_latch_1_writeregister_2, id_ex_latch_1_rt_2, id_ex_latch_1_writeregister_2,
       id_section_1_rt, id_section_1_writeregister, mem_wb_latch_1_writeregister_2;
  wire [3:0] ex_mem_latch_1_alu_out_2, ex_mem_latch_1_alu_out_2_2, ex_mem_latch_1_alu_out_2_3,
       ex_mem_latch_1_alu_out_2_4, ex_section_1_alu_out, ex_section_1_alu_out_2, ex_section_1_alu_out_3,
       ex_section_1_alu_out_4, id_ex_latch_1_alu_op_2, id_ex_latch_1_shamt_2, id_section_1_aluop,
       id_section_1_shamt, wb_section_1_leddisplayout, wb_section_1_leddisplayout_2,
       wb_section_1_leddisplayout_3, wb_section_1_leddisplayout_4;
  wire [5:0] ex_mem_latch_1_wb_ctrl_2, id_ex_latch_1_ex_ctrl_2, id_ex_latch_1_wb_ctrl_2,
       id_section_1_ex_ctrl, id_section_1_wb_ctrl, mem_wb_latch_1_wb_ctrl_2;
  wire [7:0] adder_1_out, alutopc_1_address, ex_mem_latch_1_pc_plus1_2, id_ex_latch_1_imm_ext_2,
       id_ex_latch_1_pc_plus1_2, id_section_1_pc_plus1_2, if_id_latch_1_pc_plus1_out,
       mem_wb_latch_1_pc_plus1_2, multiplexer_1_out, PC_q;
  wire [15:0] ex_mem_latch_1_readdata1_2, ex_mem_latch_1_readdata2_2, ex_mem_latch_1_shifter_out_2,
       ex_section_1_shifter_out, id_ex_latch_1_readdata1_2, id_ex_latch_1_readdata2_2, id_section_1_imm_ext,
       id_section_1_readdata1, id_section_1_readdata2, if_id_latch_1_instruction_out,
       mem_wb_latch_1_alu_out_2, mem_wb_latch_1_data_out_2, mem_wb_latch_1_readdata1_2,
       mem_wb_latch_1_shifter_out_2, multiplexer_2_out, multiplexer_3_out, multiplexer_4_out, ram_1_data,
       rom_1_data, wb_section_1_writedata;
  wire [15:8] id_ex_latch_1_imm_ext_2_2;

  Multiplexer #(.width(8), .enable("false")) multiplexer_1 (
    .in0(adder_1_out), .in1(id_ex_latch_1_imm_ext_2), .out(multiplexer_1_out), .sel(ex_section_1_branch));
  Clock clock_1 (.out(clock_1_out));
  Register PC (.D(multiplexer_1_out), .Q(PC_q), .clk(or_1_out), .clr(button_1_out));  // open: en
  Button button_1 (.out(button_1_out));
  and and_1 (and_1_out, clock_1_out, not_1_out);
  not not_1 (not_1_out, wb_section_1_halt);
  Adder adder_1 (.a(PC_q), .b(8'h1), .out(adder_1_out));  // open: cin, cout
  or or_1 (or_1_out, and_1_out, hazarddetect_1_hazard);
  ROM #(.dataWidth(16)) rom_1 (.addr(PC_q), .data(rom_1_data), .sel(1'b1));
  Hex_Digit_Display hex_digit_display_1 (.value(wb_section_1_leddisplayout_3));  // open: dp
  Hex_Digit_Display hex_digit_display_2 (.value(wb_section_1_leddisplayout_4));  // open: dp
  LED Halt (.in(wb_section_1_halt));
  Hex_Digit_Display hex_digit_display_3 (.value(wb_section_1_leddisplayout_2));  // open: dp
  Hex_Digit_Display hex_digit_display_4 (.value(wb_section_1_leddisplayout));  // open: dp
  IF_ID_LATCH if_id_latch_1 (
    .Instruction_IN(rom_1_data), .PC_PLUS1_IN(adder_1_out), .Clock(or_1_out),
    .Instruction_OUT(if_id_latch_1_instruction_out), .PC_PLUS1_OUT(if_id_latch_1_pc_plus1_out),
    .Bubble(ex_section_1_branch));
  ID_SECTION id_section_1 (
    .Instruction(if_id_latch_1_instruction_out), .Clock(and_1_out),
    .WriteReg(mem_wb_latch_1_writeregister_2), .WriteData(wb_section_1_writedata),
    .WriteEnable(wb_section_1_writeenable), .PC_PLUS1(if_id_latch_1_pc_plus1_out),
    .Subop(id_section_1_subop), .PC_PLUS1_2(id_section_1_pc_plus1_2), .ReadData1(id_section_1_readdata1),
    .ReadData2(id_section_1_readdata2), .IMM_ext(id_section_1_imm_ext),
    .WriteRegister(id_section_1_writeregister), .Shamt(id_section_1_shamt), .ALUOp(id_section_1_aluop),
    .EX_CTRL(id_section_1_ex_ctrl), .MemWrite(id_section_1_memwrite), .MemRead(id_section_1_memread),
    .WB_CTRL(id_section_1_wb_ctrl), .Rt(id_section_1_rt));
  Hex_Digit_Display hex_digit_display_5 (.value(wb_section_1_writedata[15:12]));  // open: dp
  HazardDetect hazarddetect_1 (
    .ID_EX_Memread(id_ex_latch_1_memread_2), .ID_EX_RT(id_ex_latch_1_writeregister_2),
    .IF_ID_RS(id_section_1_rt), .IF_ID_RT(id_section_1_writeregister), .Hazard(hazarddetect_1_hazard));
  Hex_Digit_Display hex_digit_display_6 (.value(wb_section_1_writedata[11:8]));  // open: dp
  Hex_Digit_Display hex_digit_display_7 (.value(wb_section_1_writedata[7:4]));  // open: dp
  Hex_Digit_Display hex_digit_display_8 (.value(wb_section_1_writedata[3:0]));  // open: dp
  or or_2 (or_2_out, hazarddetect_1_hazard, ex_section_1_branch);
  ID_EX_LATCH id_ex_latch_1 (
    .ALU_Op(id_section_1_aluop), .Subop(id_section_1_subop), .ReadData1(id_section_1_readdata1),
    .Shamt(id_section_1_shamt), .ReadData2(id_section_1_readdata2), .IMM_ext(id_section_1_imm_ext),
    .EX_CTRL(id_section_1_ex_ctrl), .MemWrite(id_section_1_memwrite), .MemRead(id_section_1_memread),
    .PC_Plus1(id_section_1_pc_plus1_2), .WriteRegister(id_section_1_writeregister),
    .WB_CTRL(id_section_1_wb_ctrl), .Clock(and_1_out), .ALU_Op_2(id_ex_latch_1_alu_op_2),
    .Subop_2(id_ex_latch_1_subop_2), .ReadData1_2(id_ex_latch_1_readdata1_2),
    .Shamt_2(id_ex_latch_1_shamt_2), .ReadData2_2(id_ex_latch_1_readdata2_2),
    .IMM_ext_2({id_ex_latch_1_imm_ext_2_2, id_ex_latch_1_imm_ext_2}), .EX_CTRL_2(id_ex_latch_1_ex_ctrl_2),
    .MemWrite_2(id_ex_latch_1_memwrite_2), .MemRead_2(id_ex_latch_1_memread_2),
    .PC_Plus1_2(id_ex_latch_1_pc_plus1_2), .WriteRegister_2(id_ex_latch_1_writeregister_2),
    .WB_CTRL_2(id_ex_latch_1_wb_ctrl_2), .Bubble(or_2_out), .Rt(id_section_1_rt), .Rt_2(id_ex_latch_1_rt_2));
  Multiplexer #(.select(2), .width(16), .enable("false")) multiplexer_2 (
    .in0(id_ex_latch_1_readdata1_2), .in1(wb_section_1_writedata),
    .in2({ex_mem_latch_1_alu_out_2_4, ex_mem_latch_1_alu_out_2_3, ex_mem_latch_1_alu_out_2_2, ex_mem_latch_1_alu_out_2}),
    .out(multiplexer_2_out), .sel(forwardunit_1_ctrl_a));  // open: in3
  Multiplexer #(.select(2), .width(16), .enable("false")) multiplexer_3 (
    .in0(id_ex_latch_1_readdata2_2), .in1(wb_section_1_writedata),
    .in2({ex_mem_latch_1_alu_out_2_4, ex_mem_latch_1_alu_out_2_3, ex_mem_latch_1_alu_out_2_2, ex_mem_latch_1_alu_out_2}),
    .out(multiplexer_3_out), .sel(forwardunit_1_ctrl_b));  // open: in3
  EX_SECTION ex_section_1 (
    .ALUOp(id_ex_latch_1_alu_op_2), .Subop(id_ex_latch_1_subop_2), .ReadData1(multiplexer_2_out),
    .Shamt(id_ex_latch_1_shamt_2), .ReadData2(multiplexer_3_out),
    .IMM_ext({id_ex_latch_1_imm_ext_2_2, id_ex_latch_1_imm_ext_2}), .EX_CTRL(id_ex_latch_1_ex_ctrl_2),
    .Branch(ex_section_1_branch),
    .ALU_OUT({ex_section_1_alu_out_4, ex_section_1_alu_out_3, ex_section_1_alu_out_2, ex_section_1_alu_out}),
    .Shifter_OUT(ex_section_1_shifter_out));
  Hex_Digit_Display hex_digit_display_9 (.value(ex_section_1_alu_out_4));  // open: dp
  ForwardUnit forwardunit_1 (
    .ID_EX_Rs(id_ex_latch_1_writeregister_2), .EX_MEM_Rs(ex_mem_latch_1_writeregister_2),
    .EX_MEM_RegWrite(ex_mem_latch_1_wb_ctrl_2[4]), .ID_EX_Rt(id_ex_latch_1_rt_2),
    .MEM_WB_Rs(mem_wb_latch_1_writeregister_2), .MEM_WB_RegWrite(wb_section_1_writeenable),
    .CTRL_A(forwardunit_1_ctrl_a), .CTRL_B(forwardunit_1_ctrl_b));
  Hex_Digit_Display hex_digit_display_10 (.value(ex_section_1_alu_out_3));  // open: dp
  Hex_Digit_Display hex_digit_display_11 (.value(ex_section_1_alu_out_2));  // open: dp
  Hex_Digit_Display hex_digit_display_12 (.value(ex_section_1_alu_out));  // open: dp
  EX_MEM_LATCH ex_mem_latch_1 (
    .ReadData1(multiplexer_2_out), .ReadData2(multiplexer_3_out), .MemWrite(id_ex_latch_1_memwrite_2),
    .MemRead(id_ex_latch_1_memread_2),
    .ALU_OUT({ex_section_1_alu_out_4, ex_section_1_alu_out_3, ex_section_1_alu_out_2, ex_section_1_alu_out}),
    .Shifter_OUT(ex_section_1_shifter_out), .PC_PLUS1(id_ex_latch_1_pc_plus1_2),
    .WriteRegister(id_ex_latch_1_writeregister_2), .WB_CTRL(id_ex_latch_1_wb_ctrl_2), .Clock(and_1_out),
    .ReadData1_2(ex_mem_latch_1_readdata1_2), .ReadData2_2(ex_mem_latch_1_readdata2_2),
    .MemRead_2(ex_mem_latch_1_memread_2),
    .ALU_OUT_2({ex_mem_latch_1_alu_out_2_4, ex_mem_latch_1_alu_out_2_3, ex_mem_latch_1_alu_out_2_2, ex_mem_latch_1_alu_out_2}),
    .Shifter_OUT_2(ex_mem_latch_1_shifter_out_2), .PC_PLUS1_2(ex_mem_latch_1_pc_plus1_2),
    .WriteRegister_2(ex_mem_latch_1_writeregister_2), .WB_CTRL_2(ex_mem_latch_1_wb_ctrl_2));  // open: MemWrite_2
  Multiplexer #(.width(16), .enable("false")) multiplexer_4 (
    .in0(multiplexer_3_out), .in1(ex_mem_latch_1_readdata2_2), .out(multiplexer_4_out),
    .sel(ex_mem_latch_1_memread_2));
  ALUtoPC alutopc_1 (.ALUOut(multiplexer_4_out), .Address(alutopc_1_address));
  Hex_Digit_Display hex_digit_display_13 (.value(ex_mem_latch_1_alu_out_2_4));  // open: dp
  RAM #(.dataWidth(16), .bus("separate")) ram_1 (
    .addr(alutopc_1_address), .din(multiplexer_2_out), .data(ram_1_data), .str(id_ex_latch_1_memwrite_2),
    .sel(1'b1), .clk(and_1_out), .ld(ex_mem_latch_1_memread_2));  // open: clr
  Hex_Digit_Display hex_digit_display_14 (.value(ex_mem_latch_1_alu_out_2_2));  // open: dp
  Hex_Digit_Display hex_digit_display_15 (.value(ex_mem_latch_1_alu_out_2_3));  // open: dp
  MEM_WB_LATCH mem_wb_latch_1 (
    .Data_OUT(ram_1_data),
    .ALU_OUT({ex_mem_latch_1_alu_out_2_4, ex_mem_latch_1_alu_out_2_3, ex_mem_latch_1_alu_out_2_2, ex_mem_latch_1_alu_out_2}),
    .Shifter_OUT(ex_mem_latch_1_shifter_out_2), .ReadData1(ex_mem_latch_1_readdata1_2),
    .PC_PLUS1(ex_mem_latch_1_pc_plus1_2), .WriteRegister(ex_mem_latch_1_writeregister_2),
    .WB_CTRL(ex_mem_latch_1_wb_ctrl_2), .Clock(and_1_out), .Data_OUT_2(mem_wb_latch_1_data_out_2),
    .ALU_OUT_2(mem_wb_latch_1_alu_out_2), .Shifter_OUT_2(mem_wb_latch_1_shifter_out_2),
    .ReadData1_2(mem_wb_latch_1_readdata1_2), .PC_PLUS1_2(mem_wb_latch_1_pc_plus1_2),
    .WriteRegister_2(mem_wb_latch_1_writeregister_2), .WB_CTRL_2(mem_wb_latch_1_wb_ctrl_2));
  Hex_Digit_Display hex_digit_display_16 (.value(ex_mem_latch_1_alu_out_2));  // open: dp
  WB_SECTION wb_section_1 (
    .Data_OUT(mem_wb_latch_1_data_out_2), .ALU_OUT(mem_wb_latch_1_alu_out_2),
    .Shifter_OUT(mem_wb_latch_1_shifter_out_2), .ReadData1(mem_wb_latch_1_readdata1_2),
    .PC_PLUS1(mem_wb_latch_1_pc_plus1_2), .Clock(and_1_out), .WriteData(wb_section_1_writedata),
    .LEDDIsplayOUT({wb_section_1_leddisplayout_4, wb_section_1_leddisplayout_3, wb_section_1_leddisplayout_2, wb_section_1_leddisplayout}),
    .WB_CTRL(mem_wb_latch_1_wb_ctrl_2), .WriteEnable(wb_section_1_writeenable), .Halt(wb_section_1_halt));
  Hex_Digit_Display hex_digit_display_17 (.value(wb_section_1_leddisplayout_4));  // open: dp
  LED Halt_2 (.in(wb_section_1_halt));
  Hex_Digit_Display hex_digit_display_18 (.value(wb_section_1_leddisplayout_2));  // open: dp
  Hex_Digit_Display hex_digit_display_19 (.value(wb_section_1_leddisplayout_3));  // open: dp
  Hex_Digit_Display hex_digit_display_20 (.value(wb_section_1_leddisplayout));  // open: dp

  // Notes on the sheet:
  //   Stall
  //   contents of rom_1 (hex, n*v repeats v):
  //   1002 1201 1402 1601 1802 1a02 1c02 1e02 280 860b 1402 1904 a20e 1c06 1a07 f400 f200 f600 fc00 7000
  //   IF/ID
  //   ID
  //   Hazard
  //   ID/EX
  //   A
  //   EX
  //   B
  //   EX/MEM
  //   EX/MEM RegWrite
  //   MEM
  //   MEM/WB
  //   WB
endmodule

module InstructionSplitter (
  input  [15:0] Instruction,
  output [3:0] Opcode,
  output [2:0] ReadRegister1,
  output [2:0] ReadRegister2,
  output [2:0] WriteRegister,
  output [3:0] ShiftAmount,
  output SubOp,
  output Unsigned,
  output [7:0] Immediate
);


  assign Immediate = Instruction[7:0];
  assign Opcode = Instruction[15:12];
  assign ReadRegister1 = Instruction[11:9];
  assign ReadRegister2 = Instruction[8:6];
  assign ShiftAmount = Instruction[4:1];
  assign SubOp = Instruction[0];
  assign Unsigned = Instruction[8];
  assign WriteRegister = Instruction[11:9];
endmodule

module SignExtend (
  input  Unsigned,
  input  [7:0] Immediate,
  output [15:0] SignExtendedImm
);

  wire [15:0] bit_extender_1_out, bit_extender_2_out;

  assign bit_extender_1_out = {{8{Immediate[7]}}, Immediate};  // Bit_Extender bit_extender_1
  assign bit_extender_2_out = {{8{1'b0}}, Immediate};  // Bit_Extender bit_extender_2
  Multiplexer #(.width(16), .disabled(0), .enable("false")) multiplexer_1 (
    .in0(bit_extender_1_out), .in1(bit_extender_2_out), .out(SignExtendedImm), .sel(Unsigned));
endmodule

module ALUtoPC (
  input  [15:0] ALUOut,
  output [7:0] Address
);


  assign Address = ALUOut[7:0];
endmodule

module Shifter (
  input  Subop,
  input  [15:0] Data,
  input  [15:0] ShamtReg,
  input  ShiftSrc,
  input  [3:0] Shamt,
  output [15:0] ShiftOut
);

  wire [3:0] multiplexer_1_out;
  wire [15:0] shifter_1_out, shifter_2_out;

  Multiplexer #(.width(4), .disabled(0), .enable("false")) multiplexer_1 (
    .in0(ShamtReg[3:0]), .in1(Shamt), .out(multiplexer_1_out), .sel(ShiftSrc));
  Shifter_part #(.width(16)) shifter_1 (.in(Data), .\dist (multiplexer_1_out), .out(shifter_1_out));
  Shifter_part #(.width(16), .shift("lr")) shifter_2 (.in(Data), .\dist (multiplexer_1_out), .out(shifter_2_out));
  Multiplexer #(.width(16), .disabled(0), .enable("false")) multiplexer_2 (
    .in0(shifter_1_out), .in1(shifter_2_out), .out(ShiftOut), .sel(Subop));
endmodule

module RegisterFile (
  input  [2:0] ReadRegister1,
  input  [2:0] ReadRegister2,
  input  [2:0] WriteRegister,
  input  [15:0] WriteData,
  input  WriteEnable,
  input  Clock,
  output [15:0] ReadData1,
  output [15:0] ReadData2
);

  wire comparator_1_eq, comparator_2_eq, decoder_1_out0, decoder_1_out1, decoder_1_out2, decoder_1_out3,
       decoder_1_out4, decoder_1_out5, decoder_1_out6, decoder_1_out7;
  wire [15:0] multiplexer_1_out, multiplexer_2_out, register_1_q, register_2_q, register_3_q, register_4_q,
       register_5_q, register_6_q, register_7_q, register_8_q;

  Decoder_part #(.select(3), .disabled(0)) decoder_1 (
    .out0(decoder_1_out0), .out1(decoder_1_out1), .out2(decoder_1_out2), .out3(decoder_1_out3),
    .out4(decoder_1_out4), .out5(decoder_1_out5), .out6(decoder_1_out6), .out7(decoder_1_out7),
    .sel(WriteRegister), .en(WriteEnable));
  Register #(.width(16)) register_1 (.D(WriteData), .en(decoder_1_out0), .Q(register_1_q), .clk(Clock));  // open: clr
  Register #(.width(16)) register_2 (.D(WriteData), .en(decoder_1_out1), .Q(register_2_q), .clk(Clock));  // open: clr
  Register #(.width(16)) register_3 (.D(WriteData), .en(decoder_1_out2), .Q(register_3_q), .clk(Clock));  // open: clr
  Register #(.width(16)) register_4 (.D(WriteData), .en(decoder_1_out3), .Q(register_4_q), .clk(Clock));  // open: clr
  Register #(.width(16)) register_5 (.D(WriteData), .en(decoder_1_out4), .Q(register_5_q), .clk(Clock));  // open: clr
  Register #(.width(16)) register_6 (.D(WriteData), .en(decoder_1_out5), .Q(register_6_q), .clk(Clock));  // open: clr
  Register #(.width(16)) register_7 (.D(WriteData), .en(decoder_1_out6), .Q(register_7_q), .clk(Clock));  // open: clr
  Register #(.width(16)) register_8 (.D(WriteData), .en(decoder_1_out7), .Q(register_8_q), .clk(Clock));  // open: clr
  Multiplexer #(.select(3), .width(16), .enable("false")) multiplexer_1 (
    .in0(register_1_q), .in1(register_2_q), .in2(register_3_q), .in3(register_4_q), .in4(register_5_q),
    .in5(register_6_q), .in6(register_7_q), .in7(register_8_q), .out(multiplexer_1_out), .sel(ReadRegister1));
  Multiplexer #(.select(3), .width(16), .enable("false")) multiplexer_2 (
    .in0(register_1_q), .in1(register_2_q), .in2(register_3_q), .in3(register_4_q), .in4(register_5_q),
    .in5(register_6_q), .in6(register_7_q), .in7(register_8_q), .out(multiplexer_2_out), .sel(ReadRegister2));
  Comparator #(.width(3)) comparator_1 (.a(ReadRegister1), .b(WriteRegister), .eq(comparator_1_eq));  // open: gt, lt
  Multiplexer #(.width(16), .enable("false")) multiplexer_3 (
    .in0(multiplexer_1_out), .in1(WriteData), .out(ReadData1), .sel(comparator_1_eq));
  Multiplexer #(.width(16), .enable("false")) multiplexer_4 (
    .in0(multiplexer_2_out), .in1(WriteData), .out(ReadData2), .sel(comparator_2_eq));
  Comparator #(.width(3)) comparator_2 (.a(ReadRegister2), .b(WriteRegister), .eq(comparator_2_eq));  // open: gt, lt
endmodule

module ShifterDecoder (
  input  [3:0] Opcode,
  output ShiftSrc,
  output ShiftertoReg,
  output RegWrite
);

  and and_1 (RegWrite, ~Opcode[3], Opcode[2], ~Opcode[1]);  // AND_Gate

  assign ShiftertoReg = RegWrite;
  assign ShiftSrc = Opcode[0];
endmodule

module Arith_Log_Decoder (
  input  [3:0] Opcode,
  input  Subop,
  output [3:0] ALUOperation,
  output RegWrite,
  output ALUSrc
);

  wire and_2_out, and_3_out, and_5_out, and_6_out, not_1_out, not_2_out, not_3_out, not_4_out, not_5_out,
       not_6_out, not_7_out, not_8_out, not_9_out, not_10_out, not_11_out, not_12_out, not_13_out,
       not_14_out, not_15_out, not_16_out, not_17_out, not_18_out, not_19_out, not_20_out, not_21_out;

  not not_1 (not_1_out, Opcode[3]);
  not not_2 (not_2_out, Opcode[2]);
  not not_3 (not_3_out, Subop);
  not not_4 (not_4_out, Opcode[3]);
  not not_5 (not_5_out, Opcode[2]);
  not not_6 (not_6_out, Opcode[1]);
  not not_7 (not_7_out, Opcode[0]);
  not not_8 (not_8_out, Opcode[3]);
  not not_9 (not_9_out, Opcode[2]);
  not not_10 (not_10_out, Subop);
  not not_11 (not_11_out, Opcode[3]);
  not not_12 (not_12_out, Opcode[2]);
  not not_13 (not_13_out, Opcode[1]);
  not not_14 (not_14_out, Opcode[3]);
  not not_15 (not_15_out, Opcode[2]);
  not not_16 (not_16_out, Opcode[1]);
  not not_17 (not_17_out, Opcode[3]);
  not not_18 (not_18_out, Opcode[2]);
  not not_19 (not_19_out, Opcode[3]);
  not not_20 (not_20_out, Opcode[2]);
  not not_21 (not_21_out, Opcode[1]);
  and and_1 (ALUOperation[3], not_1_out, not_2_out, Opcode[1], Opcode[0], not_3_out);
  and and_2 (and_2_out, not_4_out, not_5_out, not_6_out, not_7_out, Subop);
  and and_3 (and_3_out, not_8_out, not_9_out, Opcode[1], Opcode[0], not_10_out);
  and and_4 (ALUOperation[1], not_11_out, not_12_out, not_13_out);
  and and_5 (and_5_out, not_14_out, not_15_out, not_16_out);
  and and_6 (and_6_out, not_17_out, not_18_out, Opcode[0]);
  and and_7 (ALUSrc, not_19_out, not_20_out, not_21_out, Opcode[0]);
  or or_1 (ALUOperation[2], and_2_out, and_3_out);
  or or_2 (RegWrite, and_5_out, and_6_out);

  assign ALUOperation[0] = 1'b0;
endmodule

module Arith_Log (
  input  Opcode3,
  input  Opcode2,
  input  Opcode1,
  input  Opcode0,
  input  Unsigned,
  input  Subop,
  output ALUOp3,
  output ALUOp2,
  output ALUOp1,
  output ALUOp0,
  output RegWrite,
  output ALUSrc
);

  wire and_2_out, and_3_out, and_5_out, and_6_out, not_1_out, not_2_out, not_3_out, not_4_out, not_5_out,
       not_6_out, not_7_out, not_8_out, not_9_out, not_10_out, not_11_out, not_12_out, not_13_out,
       not_14_out, not_15_out, not_16_out, not_17_out, not_18_out, not_19_out, not_20_out, not_21_out;

  not not_1 (not_1_out, Opcode3);
  not not_2 (not_2_out, Opcode2);
  not not_3 (not_3_out, Subop);
  not not_4 (not_4_out, Opcode3);
  not not_5 (not_5_out, Opcode2);
  not not_6 (not_6_out, Opcode1);
  not not_7 (not_7_out, Opcode0);
  not not_8 (not_8_out, Opcode3);
  not not_9 (not_9_out, Opcode2);
  not not_10 (not_10_out, Subop);
  not not_11 (not_11_out, Opcode3);
  not not_12 (not_12_out, Opcode2);
  not not_13 (not_13_out, Opcode1);
  not not_14 (not_14_out, Opcode3);
  not not_15 (not_15_out, Opcode2);
  not not_16 (not_16_out, Opcode1);
  not not_17 (not_17_out, Opcode3);
  not not_18 (not_18_out, Opcode2);
  not not_19 (not_19_out, Opcode3);
  not not_20 (not_20_out, Opcode2);
  not not_21 (not_21_out, Opcode1);
  and and_1 (ALUOp3, not_1_out, not_2_out, Opcode1, Opcode0, not_3_out);
  and and_2 (and_2_out, not_4_out, not_5_out, not_6_out, not_7_out, Subop);
  and and_3 (and_3_out, not_8_out, not_9_out, Opcode1, Opcode0, not_10_out);
  and and_4 (ALUOp1, not_11_out, not_12_out, not_13_out);
  and and_5 (and_5_out, not_14_out, not_15_out, not_16_out);
  and and_6 (and_6_out, not_17_out, not_18_out, Opcode0);
  and and_7 (ALUSrc, not_19_out, not_20_out, not_21_out, Opcode0);
  or or_1 (ALUOp2, and_2_out, and_3_out);
  or or_2 (RegWrite, and_5_out, and_6_out);

  assign ALUOp0 = 1'b0;
endmodule

module one_bit_ALU (
  input  Ainvert,
  input  Binvert,
  input  CarryIn,
  input  [1:0] Operation,
  input  a,
  input  b,
  input  Less,
  output Result,
  output Set,
  output CarryOut
);

  wire and_1_out, multiplexer_1_out, multiplexer_2_out, not_1_out, not_2_out, or_1_out;

  not not_1 (not_1_out, a);
  Multiplexer #(.enable("false")) multiplexer_1 (.in0(a), .in1(not_1_out), .out(multiplexer_1_out), .sel(Ainvert));
  not not_2 (not_2_out, b);
  Multiplexer #(.enable("false")) multiplexer_2 (.in0(b), .in1(not_2_out), .out(multiplexer_2_out), .sel(Binvert));
  and and_1 (and_1_out, multiplexer_1_out, multiplexer_2_out);
  or or_1 (or_1_out, multiplexer_1_out, multiplexer_2_out);
  Adder #(.width(1)) adder_1 (.a(multiplexer_1_out), .b(multiplexer_2_out), .out(Set), .cin(CarryIn), .cout(CarryOut));
  Multiplexer #(.select(2), .enable("false")) multiplexer_3 (
    .in0(and_1_out), .in1(or_1_out), .in2(Set), .in3(Less), .out(Result), .sel(Operation));
endmodule

module sixteen_bit_ALU (
  input  [3:0] ALUOperation,
  input  [15:0] a,
  input  [15:0] b,
  output [15:0] Result,
  output Zero,
  output Overflow
);

  wire one_bit_alu_1_carryout, one_bit_alu_2_carryout, one_bit_alu_3_carryout, one_bit_alu_4_carryout,
       one_bit_alu_5_carryout, one_bit_alu_6_carryout, one_bit_alu_7_carryout, one_bit_alu_8_carryout,
       one_bit_alu_9_carryout, one_bit_alu_10_carryout, one_bit_alu_11_carryout, one_bit_alu_12_carryout,
       one_bit_alu_13_carryout, one_bit_alu_14_carryout, one_bit_alu_15_carryout, one_bit_alu_16_carryout,
       one_bit_alu_16_set, xor_1_out;

  one_bit_ALU one_bit_alu_1 (
    .a(a[0]), .b(b[0]), .Less(xor_1_out), .Ainvert(ALUOperation[3]), .Binvert(ALUOperation[2]),
    .CarryIn(ALUOperation[2]), .Operation(ALUOperation[1:0]), .CarryOut(one_bit_alu_1_carryout),
    .Result(Result[0]));  // open: Set
  one_bit_ALU one_bit_alu_2 (
    .a(a[1]), .b(b[1]), .Less(1'b0), .Ainvert(ALUOperation[3]), .Binvert(ALUOperation[2]),
    .CarryIn(one_bit_alu_1_carryout), .Operation(ALUOperation[1:0]), .CarryOut(one_bit_alu_2_carryout),
    .Result(Result[1]));  // open: Set
  one_bit_ALU one_bit_alu_3 (
    .a(a[2]), .b(b[2]), .Less(1'b0), .Ainvert(ALUOperation[3]), .Binvert(ALUOperation[2]),
    .CarryIn(one_bit_alu_2_carryout), .Operation(ALUOperation[1:0]), .CarryOut(one_bit_alu_3_carryout),
    .Result(Result[2]));  // open: Set
  one_bit_ALU one_bit_alu_4 (
    .a(a[3]), .b(b[3]), .Less(1'b0), .Ainvert(ALUOperation[3]), .Binvert(ALUOperation[2]),
    .CarryIn(one_bit_alu_3_carryout), .Operation(ALUOperation[1:0]), .CarryOut(one_bit_alu_4_carryout),
    .Result(Result[3]));  // open: Set
  one_bit_ALU one_bit_alu_5 (
    .a(a[4]), .b(b[4]), .Less(1'b0), .Ainvert(ALUOperation[3]), .Binvert(ALUOperation[2]),
    .CarryIn(one_bit_alu_4_carryout), .Operation(ALUOperation[1:0]), .CarryOut(one_bit_alu_5_carryout),
    .Result(Result[4]));  // open: Set
  one_bit_ALU one_bit_alu_6 (
    .a(a[5]), .b(b[5]), .Less(1'b0), .Ainvert(ALUOperation[3]), .Binvert(ALUOperation[2]),
    .CarryIn(one_bit_alu_5_carryout), .Operation(ALUOperation[1:0]), .CarryOut(one_bit_alu_6_carryout),
    .Result(Result[5]));  // open: Set
  one_bit_ALU one_bit_alu_7 (
    .a(a[6]), .b(b[6]), .Less(1'b0), .Ainvert(ALUOperation[3]), .Binvert(ALUOperation[2]),
    .CarryIn(one_bit_alu_6_carryout), .Operation(ALUOperation[1:0]), .CarryOut(one_bit_alu_7_carryout),
    .Result(Result[6]));  // open: Set
  one_bit_ALU one_bit_alu_8 (
    .a(a[7]), .b(b[7]), .Less(1'b0), .Ainvert(ALUOperation[3]), .Binvert(ALUOperation[2]),
    .CarryIn(one_bit_alu_7_carryout), .Operation(ALUOperation[1:0]), .CarryOut(one_bit_alu_8_carryout),
    .Result(Result[7]));  // open: Set
  one_bit_ALU one_bit_alu_9 (
    .a(a[8]), .b(b[8]), .Less(1'b0), .Ainvert(ALUOperation[3]), .Binvert(ALUOperation[2]),
    .CarryIn(one_bit_alu_8_carryout), .Operation(ALUOperation[1:0]), .CarryOut(one_bit_alu_9_carryout),
    .Result(Result[8]));  // open: Set
  one_bit_ALU one_bit_alu_10 (
    .a(a[9]), .b(b[9]), .Less(1'b0), .Ainvert(ALUOperation[3]), .Binvert(ALUOperation[2]),
    .CarryIn(one_bit_alu_9_carryout), .Operation(ALUOperation[1:0]), .CarryOut(one_bit_alu_10_carryout),
    .Result(Result[9]));  // open: Set
  one_bit_ALU one_bit_alu_11 (
    .a(a[10]), .b(b[10]), .Less(1'b0), .Ainvert(ALUOperation[3]), .Binvert(ALUOperation[2]),
    .CarryIn(one_bit_alu_10_carryout), .Operation(ALUOperation[1:0]), .CarryOut(one_bit_alu_11_carryout),
    .Result(Result[10]));  // open: Set
  one_bit_ALU one_bit_alu_12 (
    .a(a[11]), .b(b[11]), .Less(1'b0), .Ainvert(ALUOperation[3]), .Binvert(ALUOperation[2]),
    .CarryIn(one_bit_alu_11_carryout), .Operation(ALUOperation[1:0]), .CarryOut(one_bit_alu_12_carryout),
    .Result(Result[11]));  // open: Set
  one_bit_ALU one_bit_alu_13 (
    .a(a[12]), .b(b[12]), .Less(1'b0), .Ainvert(ALUOperation[3]), .Binvert(ALUOperation[2]),
    .CarryIn(one_bit_alu_12_carryout), .Operation(ALUOperation[1:0]), .CarryOut(one_bit_alu_13_carryout),
    .Result(Result[12]));  // open: Set
  one_bit_ALU one_bit_alu_14 (
    .a(a[13]), .b(b[13]), .Less(1'b0), .Ainvert(ALUOperation[3]), .Binvert(ALUOperation[2]),
    .CarryIn(one_bit_alu_13_carryout), .Operation(ALUOperation[1:0]), .CarryOut(one_bit_alu_14_carryout),
    .Result(Result[13]));  // open: Set
  one_bit_ALU one_bit_alu_15 (
    .a(a[14]), .b(b[14]), .Less(1'b0), .Ainvert(ALUOperation[3]), .Binvert(ALUOperation[2]),
    .CarryIn(one_bit_alu_14_carryout), .Operation(ALUOperation[1:0]), .CarryOut(one_bit_alu_15_carryout),
    .Result(Result[14]));  // open: Set
  one_bit_ALU one_bit_alu_16 (
    .a(a[15]), .b(b[15]), .Less(1'b0), .Ainvert(ALUOperation[3]), .Binvert(ALUOperation[2]),
    .CarryIn(one_bit_alu_15_carryout), .Operation(ALUOperation[1:0]), .CarryOut(one_bit_alu_16_carryout),
    .Result(Result[15]), .Set(one_bit_alu_16_set));
  xor xor_1 (xor_1_out, one_bit_alu_16_set, Overflow);
  xor xor_2 (Overflow, one_bit_alu_15_carryout, one_bit_alu_16_carryout);
  nor nor_1 (Zero, Result[0], Result[1], Result[2], Result[3], Result[4], Result[5], Result[6], Result[7], Result[8], Result[9], Result[10], Result[11], Result[12], Result[13], Result[14], Result[15]);
endmodule

module PCDecoder (
  input  [3:0] Opcode,
  input  Subop,
  input  Zero,
  input  Less,
  output RegtoPC,
  output IMMtoPC,
  output ZerosToALU,
  output [3:0] ALUOp
);

  wire and_4_out, and_5_out, and_6_out, and_7_out, and_8_out, not_1_out, not_2_out, not_3_out, not_4_out,
       not_5_out, not_6_out, not_7_out, not_8_out, not_9_out, not_10_out, not_11_out, not_12_out, not_13_out,
       not_14_out, not_15_out, not_16_out;

  not not_1 (not_1_out, Opcode[2]);
  not not_2 (not_2_out, Opcode[1]);
  not not_3 (not_3_out, Subop);
  not not_4 (not_4_out, Opcode[2]);
  not not_5 (not_5_out, Opcode[1]);
  not not_6 (not_6_out, Opcode[0]);
  not not_7 (not_7_out, Opcode[2]);
  not not_8 (not_8_out, Opcode[1]);
  not not_9 (not_9_out, Zero);
  not not_10 (not_10_out, Opcode[2]);
  not not_11 (not_11_out, Zero);
  not not_12 (not_12_out, Opcode[0]);
  not not_13 (not_13_out, Zero);
  not not_14 (not_14_out, Less);
  not not_15 (not_15_out, Opcode[0]);
  and and_1 (ZerosToALU, Opcode[3], not_16_out);
  not not_16 (not_16_out, Opcode[2]);
  and and_2 (ALUOp[1], Opcode[3], not_1_out);
  and and_3 (RegtoPC, Opcode[3], Opcode[2], not_2_out, Opcode[0], not_3_out);
  and and_4 (and_4_out, Opcode[3], not_4_out, not_5_out, not_6_out, Zero);
  and and_5 (and_5_out, Opcode[3], not_7_out, not_8_out, Opcode[0], not_9_out);
  and and_6 (and_6_out, Opcode[3], not_10_out, Opcode[0], not_11_out, Less);
  and and_7 (and_7_out, Opcode[3], Opcode[1], not_12_out, not_13_out, not_14_out);
  and and_8 (and_8_out, Opcode[3], Opcode[2], Opcode[1], not_15_out);
  or or_1 (IMMtoPC, and_4_out, and_5_out, and_6_out, and_7_out, and_8_out);

  assign {ALUOp[3:2], ALUOp[0]} = 3'b000;
endmodule

module PCDecoderLogic (
  input  Opcode3,
  input  Opcode2,
  input  Opcode1,
  input  Opcode0,
  input  Subop,
  input  Zero,
  input  Less,
  output RegtoPC,
  output IMMtoPC,
  output OnestoALU
);

  wire and_2_out, and_3_out, and_4_out, and_5_out, and_6_out, not_1_out, not_2_out, not_3_out, not_4_out,
       not_5_out, not_6_out, not_7_out, not_8_out, not_9_out, not_10_out, not_11_out, not_12_out, not_13_out,
       not_14_out, not_15_out;

  not not_1 (not_1_out, Opcode1);
  not not_2 (not_2_out, Subop);
  not not_3 (not_3_out, Opcode2);
  not not_4 (not_4_out, Opcode1);
  not not_5 (not_5_out, Opcode0);
  not not_6 (not_6_out, Opcode2);
  not not_7 (not_7_out, Opcode1);
  not not_8 (not_8_out, Zero);
  not not_9 (not_9_out, Opcode2);
  not not_10 (not_10_out, Zero);
  not not_11 (not_11_out, Opcode0);
  not not_12 (not_12_out, Zero);
  not not_13 (not_13_out, Less);
  not not_14 (not_14_out, Opcode0);
  not not_15 (not_15_out, Opcode2);
  and and_1 (RegtoPC, Opcode3, Opcode2, not_1_out, Opcode0, not_2_out);
  and and_2 (and_2_out, Opcode3, not_3_out, not_4_out, not_5_out, Zero);
  and and_3 (and_3_out, Opcode3, not_6_out, not_7_out, Opcode0, not_8_out);
  and and_4 (and_4_out, Opcode3, not_9_out, Opcode0, not_10_out, Less);
  and and_5 (and_5_out, Opcode3, Opcode1, not_11_out, not_12_out, not_13_out);
  and and_6 (and_6_out, Opcode3, Opcode2, Opcode1, not_14_out);
  and and_7 (OnestoALU, Opcode3, not_15_out);
  or or_1 (IMMtoPC, and_2_out, and_3_out, and_4_out, and_5_out, and_6_out);
endmodule

module Decoder (
  input  [3:0] Opcode,
  input  Subop,
  input  Zero,
  input  Less,
  output ShiftSrc,
  output ShifterToReg,
  output RegWrite,
  output [3:0] ALUOp,
  output IMMtoALU,
  output RegtoPC,
  output IMMtoPC,
  output ZerosToALU,
  output MemWrite,
  output MemtoReg,
  output Halt,
  output LED,
  output WriteLED,
  output MemRead,
  output PCtoReg
);

  wire Arith_LogDecoder_regwrite, JALDecoder_immtopc, JALDecoder_regwrite, MemDecoder_regwrite,
       PCDecoder_immtopc, ShifterDecoder_regwrite;
  wire [3:0] Arith_LogDecoder_aluoperation, PCDecoder_aluop;

  ShifterDecoder ShifterDecoder (
    .Opcode(Opcode), .ShiftSrc(ShiftSrc), .ShiftertoReg(ShifterToReg), .RegWrite(ShifterDecoder_regwrite));
  Arith_Log_Decoder Arith_LogDecoder (
    .Opcode(Opcode), .Subop(Subop), .ALUOperation(Arith_LogDecoder_aluoperation),
    .RegWrite(Arith_LogDecoder_regwrite), .ALUSrc(IMMtoALU));
  PCDecoder PCDecoder (
    .Opcode(Opcode), .Subop(Subop), .Zero(Zero), .Less(Less), .RegtoPC(RegtoPC), .IMMtoPC(PCDecoder_immtopc),
    .ZerosToALU(ZerosToALU), .ALUOp(PCDecoder_aluop));
  MemDecoder MemDecoder (
    .Opcode(Opcode), .Subop(Subop), .MemWrite(MemWrite), .MemtoReg(MemtoReg), .RegWrite(MemDecoder_regwrite),
    .MemRead(MemRead));
  HaltDecoder haltdecoder_1 (.Opcode(Opcode), .Halt(Halt), .LED(LED));
  PutDecoder PutDecoder (.Opcode(Opcode), .WriteLED(WriteLED));
  JALDecoder JALDecoder (
    .Opcode(Opcode), .IMMtoPC(JALDecoder_immtopc), .PCtoReg(PCtoReg), .RegWrite(JALDecoder_regwrite));
  or or_1 (RegWrite, ShifterDecoder_regwrite, Arith_LogDecoder_regwrite, MemDecoder_regwrite, JALDecoder_regwrite);
  or or_2 (IMMtoPC, PCDecoder_immtopc, JALDecoder_immtopc);
  assign ALUOp = Arith_LogDecoder_aluoperation | PCDecoder_aluop;  // OR_Gate or_3, 4 bits wide
endmodule

module MemDecoder (
  input  [3:0] Opcode,
  input  Subop,
  output MemWrite,
  output MemtoReg,
  output RegWrite,
  output MemRead
);

  and and_1 (MemWrite, ~Opcode[0], Opcode[1], Opcode[2], ~Opcode[3], Subop);  // AND_Gate
  and and_2 (MemRead, ~Opcode[0], Opcode[1], Opcode[2], ~Opcode[3], ~Subop);  // AND_Gate

  assign MemtoReg = MemRead;
  assign RegWrite = MemRead;
endmodule

module HaltDecoder (
  input  [3:0] Opcode,
  output Halt,
  output LED
);

  and and_1 (Halt, ~Opcode[3], Opcode[2], Opcode[1], Opcode[0]);  // AND_Gate

  assign LED = Halt;
endmodule

module PutDecoder (
  input  [3:0] Opcode,
  output WriteLED
);

  and and_1 (WriteLED, Opcode[0], Opcode[1], Opcode[2], Opcode[3]);
endmodule

module JALDecoder (
  input  [3:0] Opcode,
  output IMMtoPC,
  output PCtoReg,
  output RegWrite
);

  and and_1 (IMMtoPC, ~Opcode[0], ~Opcode[1], Opcode[2], Opcode[3]);  // AND_Gate

  assign PCtoReg = IMMtoPC;
  assign RegWrite = IMMtoPC;
endmodule

module ResultToLess (
  input  [15:0] Result,
  output Less
);


  assign Less = Result[15];
endmodule

module ID_SECTION (
  input  [15:0] Instruction,
  input  Clock,
  input  [2:0] WriteReg,
  input  [15:0] WriteData,
  input  WriteEnable,
  input  [7:0] PC_PLUS1,
  output [5:0] EX_CTRL,
  output MemWrite,
  output MemRead,
  output [5:0] WB_CTRL,
  output [3:0] ALUOp,
  output Subop,
  output [7:0] PC_PLUS1_2,
  output [15:0] ReadData1,
  output [2:0] WriteRegister,
  output [15:0] ReadData2,
  output [3:0] Shamt,
  output [15:0] IMM_ext,
  output [2:0] Rt
);

  wire Instruction_Splitter_unsigned;
  wire [2:0] Instruction_Splitter_readregister1;
  wire [3:0] Instruction_Splitter_opcode;
  wire [7:0] Instruction_Splitter_immediate;

  InstructionSplitter Instruction_Splitter (
    .Instruction(Instruction), .Opcode(Instruction_Splitter_opcode),
    .ReadRegister1(Instruction_Splitter_readregister1), .ReadRegister2(Rt), .WriteRegister(WriteRegister),
    .ShiftAmount(Shamt), .SubOp(Subop), .Unsigned(Instruction_Splitter_unsigned),
    .Immediate(Instruction_Splitter_immediate));
  Control control_1 (
    .Opcode(Instruction_Splitter_opcode), .Subop(Subop), .EX_CTRL(EX_CTRL), .MemWrite(MemWrite),
    .MemRead(MemRead), .WB_CTRL(WB_CTRL), .ALUOp(ALUOp));
  RegisterFile Registers (
    .ReadRegister1(Instruction_Splitter_readregister1), .ReadRegister2(Rt), .WriteRegister(WriteReg),
    .WriteData(WriteData), .WriteEnable(WriteEnable), .Clock(Clock), .ReadData1(ReadData1),
    .ReadData2(ReadData2));
  SignExtend Sign_Extend (
    .Unsigned(Instruction_Splitter_unsigned), .Immediate(Instruction_Splitter_immediate),
    .SignExtendedImm(IMM_ext));

  assign PC_PLUS1_2 = PC_PLUS1;

  // Notes on the sheet:
  //   Control
endmodule

module side (
  input  Op3,
  input  Op2,
  input  Op1,
  input  Op0,
  output Op3_2,
  output Op2_2,
  output Op1_2,
  output Op0_2
);

  wire not_1_out;

  and and_1 (Op1_2, Op3, not_1_out);
  not not_1 (not_1_out, Op2);

  assign Op0_2 = 1'b0;
  assign Op2_2 = 1'b0;
  assign Op3_2 = 1'b0;
endmodule

module IF_ID_LATCH (
  input  [15:0] Instruction_IN,
  input  [7:0] PC_PLUS1_IN,
  input  Clock,
  input  Bubble,
  output [15:0] Instruction_OUT,
  output [7:0] PC_PLUS1_OUT
);

  wire [15:0] multiplexer_1_out;

  Multiplexer #(.width(16), .enable("false")) multiplexer_1 (
    .in0(Instruction_IN), .in1(16'h1000), .out(multiplexer_1_out), .sel(Bubble));
  Register #(.width(16)) register_1 (.D(multiplexer_1_out), .Q(Instruction_OUT), .clk(Clock));  // open: en, clr
  Register register_2 (.D(PC_PLUS1_IN), .Q(PC_PLUS1_OUT), .clk(Clock));  // open: en, clr
endmodule

module ID_EX_LATCH (
  input  [3:0] ALU_Op,
  input  Subop,
  input  [15:0] ReadData1,
  input  [3:0] Shamt,
  input  [15:0] ReadData2,
  input  [15:0] IMM_ext,
  input  [5:0] EX_CTRL,
  input  MemWrite,
  input  MemRead,
  input  [7:0] PC_Plus1,
  input  [2:0] WriteRegister,
  input  [5:0] WB_CTRL,
  input  [2:0] Rt,
  input  Clock,
  input  Bubble,
  output [3:0] ALU_Op_2,
  output Subop_2,
  output [15:0] ReadData1_2,
  output [3:0] Shamt_2,
  output [15:0] ReadData2_2,
  output [15:0] IMM_ext_2,
  output [5:0] EX_CTRL_2,
  output MemWrite_2,
  output MemRead_2,
  output [7:0] PC_Plus1_2,
  output [2:0] WriteRegister_2,
  output [5:0] WB_CTRL_2,
  output [2:0] Rt_2
);

  wire and_2_out;
  wire [5:0] and_1_out, and_3_out;
  wire [5:5] not_1_out;

  assign and_1_out = EX_CTRL & {6{not_1_out[5]}};  // AND_Gate and_1, 6 bits wide
  and and_2 (and_2_out, MemWrite, not_1_out[5]);
  assign and_3_out = WB_CTRL & {6{not_1_out[5]}};  // AND_Gate and_3, 6 bits wide
  not not_1 (not_1_out[5], Bubble);
  Register #(.width(4)) register_1 (.D(ALU_Op), .Q(ALU_Op_2), .clk(Clock));  // open: en, clr
  Register #(.width(1)) register_2 (.D(Subop), .Q(Subop_2), .clk(Clock));  // open: en, clr
  Register #(.width(16)) register_3 (.D(ReadData1), .Q(ReadData1_2), .clk(Clock));  // open: en, clr
  Register #(.width(4)) register_4 (.D(Shamt), .Q(Shamt_2), .clk(Clock));  // open: en, clr
  Register #(.width(16)) register_5 (.D(ReadData2), .Q(ReadData2_2), .clk(Clock));  // open: en, clr
  Register #(.width(16)) register_6 (.D(IMM_ext), .Q(IMM_ext_2), .clk(Clock));  // open: en, clr
  Register #(.width(6)) register_7 (.D(and_1_out), .Q(EX_CTRL_2), .clk(Clock));  // open: en, clr
  Register #(.width(1)) register_8 (.D(and_2_out), .Q(MemWrite_2), .clk(Clock));  // open: en, clr
  Register #(.width(1)) register_9 (.D(MemRead), .Q(MemRead_2), .clk(Clock));  // open: en, clr
  Register register_10 (.D(PC_Plus1), .Q(PC_Plus1_2), .clk(Clock));  // open: en, clr
  Register #(.width(3)) register_11 (.D(WriteRegister), .Q(WriteRegister_2), .clk(Clock));  // open: en, clr
  Register #(.width(6)) register_12 (.D(and_3_out), .Q(WB_CTRL_2), .clk(Clock));  // open: en, clr
  Register #(.width(3)) register_13 (.D(Rt), .Q(Rt_2), .clk(Clock));  // open: en, clr
endmodule

module IF_SECTION (
);

  wire button_1_out, not_1_out, undriven_2;
  wire [7:0] adder_1_out, PC_q, undriven;

  Register PC (.D(undriven), .en(not_1_out), .Q(PC_q), .clr(button_1_out));  // open: clk
  not not_1 (not_1_out, undriven_2);
  Button button_1 (.out(button_1_out));
  Adder adder_1 (.a(PC_q), .b(8'h1), .out(adder_1_out));  // open: cin, cout
  ROM #(.dataWidth(16)) rom_1 (.addr(PC_q), .sel(1'b1));  // open: data

  // Notes on the sheet:
  //   contents of rom_1 (hex, n*v repeats v):
  //   1 1104 241 1303 40 f000 241 1300 481 1503 281 6c1 1705 2c1 f200 901 1900 18ff f800 b41 1bf0 1b0f
  //   fa00 d81 1d19 fc1 1f20 3dc0 fc00 1 11e0 241 1378 3041 f000 481 150d 6c1 1708 44c0 f400 901 1910 b41
  //   1b04 4941 f800 d81 1d02 5c02 fc00 fc1 1f10 5e03 fe00 1 1140 61c1 63c0 f200 481 15ff 6c1 1701 845b
  //   865b 901 1900 985f b41 1b00 d81 1d00 1ce9 aa63 ac63 fc1 1f00 1 1119 be67 b067 e054 7000 c259 6c1
  //   170a f600 7000 d200 7000 fc1 1f01 fe00 7000 fc1 1f02 fe00 7000 fc1 1f03 fe00 7000 fc1 1f04 fe00 7000
endmodule

module Control (
  input  [3:0] Opcode,
  input  Subop,
  output [3:0] ALUOp,
  output [5:0] EX_CTRL,
  output MemWrite,
  output MemRead,
  output [5:0] WB_CTRL
);

  wire not_1_out, not_2_out, not_3_out, not_4_out, not_5_out;
  wire [3:0] Arith_LogDecoder_aluoperation, PCDecoder_aluop;

  Arith_Log_Decoder Arith_LogDecoder (
    .Opcode(Opcode), .Subop(Subop), .ALUOperation(Arith_LogDecoder_aluoperation));  // open: RegWrite, ALUSrc
  WB_CTRL wb_ctrl_1 (
    .ALUOP_3(Opcode[3]), .ALUOP_2(Opcode[2]), .ALUOP_1(Opcode[1]), .ALUOP_0(Opcode[0]), .Subop(Subop),
    .MemtoReg(WB_CTRL[0]), .PCtoReg(WB_CTRL[1]), .ShiftertoReg(WB_CTRL[2]), .WriteLED(WB_CTRL[3]),
    .WriteEnable(WB_CTRL[4]), .Halt(WB_CTRL[5]));
  EX_CTRL ex_ctrl_1 (
    .OP_3(Opcode[3]), .OP_2(Opcode[2]), .OP_1(Opcode[1]), .OP_0(Opcode[0]), .ShiftSrc(EX_CTRL[0]),
    .IMMtoALU(EX_CTRL[1]), .ZeroestoALU(EX_CTRL[2]), .Branch(EX_CTRL[3]), .EzEp(EX_CTRL[4]), .Mult(EX_CTRL[5]));
  not not_1 (not_1_out, Subop);
  PCDecoder PCDecoder (
    .Opcode(Opcode), .ALUOp(PCDecoder_aluop));  // open: Subop, Zero, Less, RegtoPC, IMMtoPC, ZerosToALU
  not not_2 (not_2_out, Opcode[0]);
  not not_3 (not_3_out, Opcode[3]);
  not not_4 (not_4_out, Opcode[0]);
  not not_5 (not_5_out, Opcode[3]);
  and and_1 (MemWrite, Subop, not_2_out, Opcode[1], Opcode[2], not_3_out);
  and and_2 (MemRead, not_1_out, not_4_out, Opcode[1], Opcode[2], not_5_out);
  assign ALUOp = Arith_LogDecoder_aluoperation | PCDecoder_aluop;  // OR_Gate or_1, 4 bits wide
endmodule

module EX_SECTION (
  input  [3:0] ALUOp,
  input  Subop,
  input  [15:0] ReadData1,
  input  [3:0] Shamt,
  input  [15:0] ReadData2,
  input  [15:0] IMM_ext,
  input  [5:0] EX_CTRL,
  output Branch,
  output [15:0] ALU_OUT,
  output [15:0] Shifter_OUT
);

  wire ALU_zero, multiplexer_4_out, not_1_out, resulttoless_1_less;
  wire [15:0] ALU_result, multiplexer_1_out, multiplexer_2_out, multiplier_1_out;

  Shifter Shifter (
    .Subop(Subop), .Data(ReadData1), .ShamtReg(ReadData2), .ShiftSrc(EX_CTRL[0]), .Shamt(Shamt),
    .ShiftOut(Shifter_OUT));
  Multiplexer #(.width(16), .enable("false")) multiplexer_1 (
    .in0(ReadData2), .in1(IMM_ext), .out(multiplexer_1_out), .sel(EX_CTRL[1]));
  Multiplexer #(.width(16), .enable("false")) multiplexer_2 (
    .in0(multiplexer_1_out), .in1({16{1'b0}}), .out(multiplexer_2_out), .sel(EX_CTRL[2]));
  sixteen_bit_ALU ALU (
    .ALUOperation(ALUOp), .a(ReadData1), .b(multiplexer_2_out), .Result(ALU_result), .Zero(ALU_zero));  // open: Overflow
  Multiplier #(.width(16)) multiplier_1 (.a(ReadData1), .b(ReadData2), .out(multiplier_1_out));  // open: cin, cout
  ResultToLess resulttoless_1 (.Result(ALU_result), .Less(resulttoless_1_less));
  Multiplexer #(.width(16), .enable("false")) multiplexer_3 (
    .in0(ALU_result), .in1(multiplier_1_out), .out(ALU_OUT), .sel(EX_CTRL[5]));
  not not_1 (not_1_out, resulttoless_1_less);
  Multiplexer #(.enable("false")) multiplexer_4 (
    .in0(not_1_out), .in1(ALU_zero), .out(multiplexer_4_out), .sel(EX_CTRL[4]));
  and and_1 (Branch, multiplexer_4_out, EX_CTRL[3]);

  // Notes on the sheet:
  //   R2/IMM
  //   EX CTRL
  //   ShiftSrc
  //   IMMtoALU
  //   ZeroestoALU
  //   Branch
  //   EZ/Ep
  //   Mult
endmodule

module MEM_SECTION (
  input  [15:0] ReadData2,
  input  [15:0] ReadData1,
  input  MemWrite,
  input  MemRead,
  input  Clock,
  output [15:0] Data_OUT
);

  wire [7:0] alutopc_1_address;

  ALUtoPC alutopc_1 (.ALUOut(ReadData2), .Address(alutopc_1_address));
  RAM #(.dataWidth(16), .bus("separate")) ram_1 (
    .addr(alutopc_1_address), .din(ReadData1), .data(Data_OUT), .str(MemWrite), .sel(1'b1), .clk(Clock),
    .ld(MemRead));  // open: clr
endmodule

module WB_SECTION (
  input  [15:0] Data_OUT,
  input  [15:0] ALU_OUT,
  input  [15:0] Shifter_OUT,
  input  [15:0] ReadData1,
  input  [7:0] PC_PLUS1,
  input  Clock,
  input  [5:0] WB_CTRL,
  output [15:0] WriteData,
  output [15:0] LEDDIsplayOUT,
  output WriteEnable,
  output Halt
);

  wire [15:0] bit_extender_1_out, multiplexer_1_out, multiplexer_2_out;

  Multiplexer #(.width(16), .enable("false")) multiplexer_1 (
    .in0(ALU_OUT), .in1(Data_OUT), .out(multiplexer_1_out), .sel(WB_CTRL[0]));
  Register #(.width(16)) register_1 (.D(ReadData1), .en(WB_CTRL[3]), .Q(LEDDIsplayOUT), .clk(Clock));  // open: clr
  Multiplexer #(.width(16), .enable("false")) multiplexer_2 (
    .in0(multiplexer_1_out), .in1(Shifter_OUT), .out(multiplexer_2_out), .sel(WB_CTRL[2]));
  assign bit_extender_1_out = {{8{1'b0}}, PC_PLUS1};  // Bit_Extender bit_extender_1
  Multiplexer #(.width(16), .enable("false")) multiplexer_3 (
    .in0(multiplexer_2_out), .in1(bit_extender_1_out), .out(WriteData), .sel(WB_CTRL[1]));

  assign Halt = WB_CTRL[5];
  assign WriteEnable = WB_CTRL[4];

  // Notes on the sheet:
  //   ShiftertoReg
  //   Halt
  //   WB CONTROL
  //   MemtoReg
  //   PctoReg
  //   WriteLed
  //   WriteEnable
endmodule

module MEM_WB_LATCH (
  input  [15:0] Data_OUT,
  input  [15:0] ALU_OUT,
  input  [15:0] Shifter_OUT,
  input  [15:0] ReadData1,
  input  [7:0] PC_PLUS1,
  input  [2:0] WriteRegister,
  input  [5:0] WB_CTRL,
  input  Clock,
  output [15:0] Data_OUT_2,
  output [15:0] ALU_OUT_2,
  output [15:0] Shifter_OUT_2,
  output [15:0] ReadData1_2,
  output [7:0] PC_PLUS1_2,
  output [2:0] WriteRegister_2,
  output [5:0] WB_CTRL_2
);

  Register #(.width(16)) register_1 (.D(Data_OUT), .Q(Data_OUT_2), .clk(Clock));  // open: en, clr
  Register #(.width(16)) register_2 (.D(ALU_OUT), .Q(ALU_OUT_2), .clk(Clock));  // open: en, clr
  Register #(.width(16)) register_3 (.D(Shifter_OUT), .Q(Shifter_OUT_2), .clk(Clock));  // open: en, clr
  Register #(.width(16)) register_4 (.D(ReadData1), .Q(ReadData1_2), .clk(Clock));  // open: en, clr
  Register register_5 (.D(PC_PLUS1), .Q(PC_PLUS1_2), .clk(Clock));  // open: en, clr
  Register #(.width(3)) register_6 (.D(WriteRegister), .Q(WriteRegister_2), .clk(Clock));  // open: en, clr
  Register #(.width(6)) register_7 (.D(WB_CTRL), .Q(WB_CTRL_2), .clk(Clock));  // open: en, clr

  // Notes on the sheet:
  //   ShiftertoReg
  //   WB CONTROL
  //   MemtoReg
  //   PctoReg
  //   WriteLed
  //   WriteEnable
endmodule

module EX_MEM_LATCH (
  input  [15:0] ReadData1,
  input  [15:0] ReadData2,
  input  MemWrite,
  input  MemRead,
  input  [15:0] ALU_OUT,
  input  [15:0] Shifter_OUT,
  input  [7:0] PC_PLUS1,
  input  [2:0] WriteRegister,
  input  [5:0] WB_CTRL,
  input  Clock,
  output [15:0] ReadData1_2,
  output [15:0] ReadData2_2,
  output MemWrite_2,
  output MemRead_2,
  output [15:0] ALU_OUT_2,
  output [15:0] Shifter_OUT_2,
  output [7:0] PC_PLUS1_2,
  output [2:0] WriteRegister_2,
  output [5:0] WB_CTRL_2
);

  Register #(.width(16)) register_1 (.D(ReadData1), .Q(ReadData1_2), .clk(Clock));  // open: en, clr
  Register #(.width(16)) register_2 (.D(ReadData2), .Q(ReadData2_2), .clk(Clock));  // open: en, clr
  Register #(.width(1)) register_3 (.D(MemWrite), .Q(MemWrite_2), .clk(Clock));  // open: en, clr
  Register #(.width(1)) register_4 (.D(MemRead), .en(MemRead), .Q(MemRead_2), .clk(Clock));  // open: clr
  Register #(.width(16)) register_5 (.D(ALU_OUT), .Q(ALU_OUT_2), .clk(Clock));  // open: en, clr
  Register #(.width(16)) register_6 (.D(Shifter_OUT), .Q(Shifter_OUT_2), .clk(Clock));  // open: en, clr
  Register register_7 (.D(PC_PLUS1), .Q(PC_PLUS1_2), .clk(Clock));  // open: en, clr
  Register #(.width(3)) register_8 (.D(WriteRegister), .Q(WriteRegister_2), .clk(Clock));  // open: en, clr
  Register #(.width(6)) register_9 (.D(WB_CTRL), .Q(WB_CTRL_2), .clk(Clock));  // open: en, clr
endmodule

module EX_CTRL (
  input  OP_3,
  input  OP_2,
  input  OP_1,
  input  OP_0,
  output ShiftSrc,
  output IMMtoALU,
  output ZeroestoALU,
  output Branch,
  output EzEp,
  output Mult
);

  wire not_1_out, not_2_out, not_3_out, not_4_out, not_5_out, not_6_out, not_7_out;

  not not_1 (not_1_out, OP_3);
  not not_2 (not_2_out, OP_2);
  not not_3 (not_3_out, OP_1);
  not not_4 (not_4_out, OP_2);
  and and_1 (ZeroestoALU, OP_3, not_4_out, not_5_out);
  not not_5 (not_5_out, OP_0);
  and and_2 (Branch, OP_3, not_6_out, not_7_out);
  not not_6 (not_6_out, OP_2);
  not not_7 (not_7_out, OP_0);
  not not_8 (EzEp, OP_1);
  and and_3 (Mult, ~OP_0, OP_1, ~OP_2, ~OP_3);  // AND_Gate
  and and_4 (IMMtoALU, not_1_out, not_2_out, not_3_out, OP_0);

  assign ShiftSrc = 1'b0;
endmodule

module WB_CTRL (
  input  ALUOP_3,
  input  ALUOP_2,
  input  ALUOP_1,
  input  ALUOP_0,
  input  Subop,
  output MemtoReg,
  output PCtoReg,
  output ShiftertoReg,
  output WriteLED,
  output WriteEnable,
  output Halt
);

  wire and_3_out, and_4_out, and_5_out, not_1_out, not_2_out, not_3_out, not_4_out, not_5_out, not_6_out,
       not_7_out, not_8_out, not_9_out, not_10_out, not_11_out, not_12_out, not_13_out;

  not not_1 (not_1_out, ALUOP_3);
  not not_2 (not_2_out, ALUOP_0);
  not not_3 (not_3_out, Subop);
  and and_1 (WriteLED, ALUOP_3, ALUOP_2, ALUOP_1, ALUOP_0);
  not not_4 (not_4_out, ALUOP_3);
  not not_5 (not_5_out, ALUOP_2);
  not not_6 (not_6_out, ALUOP_1);
  not not_7 (not_7_out, ALUOP_3);
  not not_8 (not_8_out, ALUOP_2);
  not not_9 (not_9_out, ALUOP_0);
  not not_10 (not_10_out, ALUOP_3);
  not not_11 (not_11_out, ALUOP_0);
  not not_12 (not_12_out, Subop);
  not not_13 (not_13_out, ALUOP_3);
  and and_2 (MemtoReg, not_1_out, ALUOP_2, ALUOP_1, not_2_out, not_3_out);
  and and_3 (and_3_out, not_4_out, not_5_out, not_6_out);
  and and_4 (and_4_out, not_7_out, not_8_out, not_9_out);
  and and_5 (and_5_out, not_10_out, ALUOP_1, not_11_out, not_12_out);
  and and_6 (Halt, not_13_out, ALUOP_2, ALUOP_1, ALUOP_0);
  or or_1 (WriteEnable, and_3_out, and_4_out, and_5_out);

  assign PCtoReg = 1'b0;
  assign ShiftertoReg = 1'b0;
endmodule

module HazardDetect (
  input  ID_EX_Memread,
  input  [2:0] ID_EX_RT,
  input  [2:0] IF_ID_RS,
  input  [2:0] IF_ID_RT,
  output Hazard
);

  wire comparator_1_eq, comparator_2_eq, or_1_out;

  Comparator #(.width(3), .mode("unsigned")) comparator_1 (
    .a(ID_EX_RT), .b(IF_ID_RS), .eq(comparator_1_eq));  // open: gt, lt
  Comparator #(.width(3), .mode("unsigned")) comparator_2 (
    .a(ID_EX_RT), .b(IF_ID_RT), .eq(comparator_2_eq));  // open: gt, lt
  or or_1 (or_1_out, comparator_1_eq, comparator_2_eq);
  and and_1 (Hazard, ID_EX_Memread, or_1_out);
endmodule

module ForwardUnit (
  input  [2:0] ID_EX_Rs,
  input  [2:0] EX_MEM_Rs,
  input  EX_MEM_RegWrite,
  input  [2:0] ID_EX_Rt,
  input  [2:0] MEM_WB_Rs,
  input  MEM_WB_RegWrite,
  output [1:0] CTRL_A,
  output [1:0] CTRL_B
);

  wire and_3_out, and_4_out, comparator_1_eq, comparator_2_eq, comparator_3_eq, comparator_4_eq;

  Comparator #(.width(3)) comparator_1 (.a(ID_EX_Rs), .b(EX_MEM_Rs), .eq(comparator_1_eq));  // open: gt, lt
  Comparator #(.width(3)) comparator_2 (.a(EX_MEM_Rs), .b(ID_EX_Rt), .eq(comparator_2_eq));  // open: gt, lt
  Comparator #(.width(3)) comparator_3 (.a(ID_EX_Rt), .b(MEM_WB_Rs), .eq(comparator_3_eq));  // open: gt, lt
  Comparator #(.width(3)) comparator_4 (.a(MEM_WB_Rs), .b(ID_EX_Rs), .eq(comparator_4_eq));  // open: gt, lt
  and and_1 (CTRL_A[1], comparator_1_eq, EX_MEM_RegWrite);
  and and_2 (CTRL_B[1], EX_MEM_RegWrite, comparator_2_eq);
  and and_3 (and_3_out, comparator_3_eq, MEM_WB_RegWrite);
  and and_4 (and_4_out, MEM_WB_RegWrite, comparator_4_eq);
  and and_5 (CTRL_A[0], ~CTRL_A[1], and_4_out);  // AND_Gate
  and and_6 (CTRL_B[0], ~CTRL_B[1], and_3_out);  // AND_Gate
endmodule
